# Fritzing sketch Untitled Sketch (saved by Fritzing 0.8.7b)
breadboards: 1

parts:
  Composant1 = Arduino Nano (Rev3.0)
  J1 = Piezo Speaker
  U2 = SWITCH_SPDT [package=kps-1290]
  U1 = LIPO-1000mAh [package=lipo-1000]  # not connected
  Composant3 = Adafruit 4-channel I2C-safe Bi-directional Logic Level Converter [part_number="Adafruit #757"]
  WeMos_D1_Mini_Battery_Shield1 = WeMos D1 Mini Battery Shield
  Composant2 = Adafruit_BMP280

nets:
  GND: Composant1.GND, J1.pin1, Composant3.GND, WeMos_D1_Mini_Battery_Shield1.G, Composant2.GND
  N1: Composant1.D6, J1.pin2
  N2: Composant1.5V, U2.P, Composant3.HV
  N3: Composant1.A5, Composant3.B2
  N4: Composant1.A4, Composant3.B1
  3V3: Composant1.3V3, Composant3.LV, Composant2.3.3V
  N5: U2.S, WeMos_D1_Mini_Battery_Shield1.5V
  N6: Composant3.A2, Composant2.SCK/SCL
  N7: Composant3.A1, Composant2.SDI/SDA

custom parts:
  Adafruit 4-channel I2C-safe Bi-directional Logic Level Converter: Because the Arduino (and Basic Stamp) are 5V devices, and most modern sensors, displays, flash cards and modes are 3.3V-only, many makers find that they need to perform level shifting/conversion to protect the 3.3V device from 5V. We do have some other handy level shifters in the shop, from the DIP 74LVC245 to the fancy bi-directional TXB0108. However, neither of these are happy to work with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
  Adafruit_BMP280: Bosch has stepped up their game with their new BMP280 sensor, an environmental sensor with temperature, barometric pressure that is the next generation upgrade to the BMP085/BMP180/BMP183. This sensor is great for all sorts of weather sensing and can even be used in both I2C and SPI! This precision sensor from Bosch is the best low-cost, precision sensing solution for measuring barometric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
